# Fritzing sketch 2. Clock fzz chart (saved by Fritzing 0.9.3b)
breadboards: 1

parts:
  Raspberry_Pi_1 = Raspberry Pi 3 [part_number=RPI-3-V1.2]
  LED1 = smd LED [color="Red (633nm)" package="1206 [SMD]"]  # not connected
  R4 = Resistor [tolerance=±5% resistance=220 package="2512 [SMD]"]
  LED2 = smd LED [color="Red (633nm)" package="1206 [SMD]"]  # not connected

nets:
  N1: Raspberry_Pi_1.GND, R4.Pin_1
